# Fritzing sketch Server_wiring (saved by Fritzing 0.9.3b)
breadboards: 1

parts:
  Componente1 = Adafruit Feather HUZZAH ESP8266 [part_number="Adafruit #2821"]
  U1 = Vibration Motor- ROB-08449 [package=vibe-motor-10mm]
  U2 = Vibration Motor- ROB-08449 [package=vibe-motor-10mm]
  U3 = Vibration Motor- ROB-08449 [package=vibe-motor-10mm]
  U4 = Vibration Motor- ROB-08449 [package=vibe-motor-10mm]
  U5 = Vibration Motor- ROB-08449 [package=vibe-motor-10mm]
  U6 = Vibration Motor- ROB-08449 [package=vibe-motor-10mm]

nets:
  N1: Componente1.GPIO12/MISO, U2.-
  N2: Componente1.GPIO13/MOSI, U3.-
  N3: Componente1.GPIO14/SCK, U1.-
  N4: Componente1.GPIO2, U5.-
  N5: Componente1.GPIO5/SCL, U4.-
  N6: Componente1.GPIO4/SDA, U6.-
  N7: U1.+, U2.+, U3.+, U4.+, U5.+, U6.+

custom parts:
  Adafruit Feather HUZZAH ESP8266: his is the Adafruit Feather HUZZAH ESP8266 - our take on an 'all-in-one' ESP8266 WiFi development board with built in USB and battery charging. Its an ESP8266 WiFi module with all the extras you need, ready to rock! We have other boards in the Feather family, check'em out here. At the Feather HUZZAH's heart is an ESP8266 WiFi microcontroller clocked at 80 MHz and at 3.3V logic. This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
